# Fritzing sketch led blinking (saved by Fritzing 0.9.3b)

parts:
  U1 = ESP32 Devkit
  LED1 = LED - 5mm [color="Red (633nm)" package="5 mm [THT]"]
  R1 = Resistor [tolerance=±5% resistance=220 package=THT]

nets:
  N1: U1.GND, R1.Pin_0
  N2: U1.D22, LED1.anode
